# Fritzing sketch Project2 (saved by Fritzing 0.8.3b)
breadboards: 1

parts:
  Part1 = Arduino Micro (Rev3)  # not connected
  R6 = Resistor [tolerance=±5% resistance=220 package=THT]
  LED4 = LED - 3mm [color="Green (570nm)" package="3 mm [THT]"]
  LED5 = LED - 3mm [color="Red (633nm)" package="3 mm [THT]"]
  LED6 = LED - 3mm [color="Green (570nm)" package="3 mm [THT]"]  # not connected
  R7 = Resistor [tolerance=±5% resistance=220 package=THT]

nets:
  N1: R6.Pin_0, R7.Pin_0
  N2: R6.Pin_1, LED4.cathode
  N3: LED5.cathode, R7.Pin_1

custom parts:
  Arduino Micro (Rev3): The GCDuino is a microcontroller board based on the ATmega328p (datasheet). It has 13 digital input/output pins (of which 6 can be used as PWM outputs and 8 as analog inputs), a 16 MHz crystal oscillator and a CP2102-4 USB PROGRAMMER connection. It contains everything needed to support the microcontroller; simply connect it to a computer with a micro USB cable to get started. It has a form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
