# Fritzing sketch Project1 (saved by Fritzing 0.8.3b)
breadboards: 1

parts:
  R1 = Resistor [tolerance=±5% resistance=220 package=THT]
  LED1 = LED - 5mm [color="Red (633nm)" package="5 mm [THT]"]
  Part1 = GCDuino v2

nets:
  N1: R1.Pin_0, Part1.GND
  N2: R1.Pin_1, LED1.cathode
  N3: LED1.anode, Part1.D11
  5V: Part1.5V, Part1.5v

custom parts:
  GCDuino v2: The GCDuino is a microcontroller board based on the ATmega328p (datasheet). It has 13 digital input/output pins (of which 6 can be used as PWM outputs and 8 as analog inputs), a 16 MHz crystal oscillator and a CP2102-4 USB PROGRAMMER connection. It has a form factor that enables it to be easily placed on a breadboard.
