# Fritzing sketch Project4 (saved by Fritzing 0.8.3b)
breadboards: 1

parts:
  R1 = Resistor [tolerance=±5% resistance=220 package=THT]
  LED1 = LED - 5mm [color="Red (633nm)" package="5 mm [THT]"]
  Part1 = GCDuino v2
  LED2 = LED - 5mm [color="Green (565nm)" package="5 mm [THT]"]
  R2 = Resistor [tolerance=±5% resistance=220 package=THT]
  S1 = Pushbutton [package="[THT]"]
  R3 = Resistor [tolerance=±5% resistance=10k package=THT]
  R4 = Rotary Potentiometer (Large) [package=THT]

nets:
  N1: R1.Pin_0, Part1.GND, R2.Pin_0, S1.Pin_1, S1.Pin_2, R4.leg1
  N2: R1.Pin_1, LED1.cathode
  N3: LED1.anode, Part1.D11
  5V: Part1.5V, Part1.5v, R3.Pin_0, R4.leg2
  N4: Part1.A0, R4.wiper
  N5: Part1.D10, LED2.anode
  N6: Part1.D13, S1.Pin_3, S1.Pin_4, R3.Pin_1
  N7: LED2.cathode, R2.Pin_1

custom parts:
  GCDuino v2: The GCDuino is a microcontroller board based on the ATmega328p (datasheet). It has 13 digital input/output pins (of which 6 can be used as PWM outputs and 8 as analog inputs), a 16 MHz crystal oscillator and a CP2102-4 USB PROGRAMMER connection. It has a form factor that enables it to be easily placed on a breadboard.
